# Fritzing sketch Neo 550's (saved by Fritzing 0.9.3b)

parts:
  BLDC1 = REV NEO 550 BLDC Motor [part_number=REV-21-1651]
  BLDC2 = REV NEO 550 BLDC Motor [part_number=REV-21-1651]
  BLDC3 = REV NEO 550 BLDC Motor [part_number=REV-21-1651]
  PDH1 = rev_pdh

nets:
  N1: BLDC1.B, PDH1.connector15
  N2: BLDC1.C, PDH1.connector14
  N3: BLDC2.B, PDH1.connector11
  N4: BLDC2.C, PDH1.connector10
  N5: BLDC3.B, PDH1.connector13
  N6: BLDC3.C, PDH1.connector12

notes:
  pretend there is a 30 amp here

custom parts:
  REV NEO 550 BLDC Motor: The REV NEO 550 Brushless Motor is the newest member in the NEO family of brushless motors. Its output power and small size are specifically designed to make NEO 550 the perfect motor for intakes and other non-drivetrain robot mechanisms. Mounting holes and pilot match a standard 550 series motor, making it natively mount to many existing off-the-shelf gearboxes.
