# Fritzing sketch Temp Swerve Base (saved by Fritzing 0.9.3b)

parts:
  PDH1 = rev_pdh
  Part1 = WCP_Kraken_X60 [part_number=19-708850]
  BLDC1 = CTRE Falcon 500 [part_number=19-708850]
  BAT1 = Battery 12V [package=battcom_20mm_pth]
  CB1 = Thermal Circuit Breaker [package=waterproof]
  Connector1 = CANcoder
  cntl1 = roborio_v2
  RPM1 = Pigeon
  CANivore1 = CANivore
  Part2 = WCP_Kraken_X60 [part_number=19-708850]
  BLDC2 = CTRE Falcon 500 [part_number=19-708850]
  Connector2 = CANcoder
  Part3 = WCP_Kraken_X60 [part_number=19-708850]
  BLDC3 = CTRE Falcon 500 [part_number=19-708850]
  Connector3 = CANcoder
  Part4 = WCP_Kraken_X60 [part_number=19-708850]
  BLDC4 = CTRE Falcon 500 [part_number=19-708850]
  Connector4 = CANcoder
  RPM2 = rev_rpm
  R1 = Resistor [tolerance=±5% resistance=220 package=THT]
  Router1 = Rounter OpenMesh
  Connector6 = Quad Connecotr

nets:
  N1: PDH1.connector12, Part4.Vin+
  N2: PDH1.connector13, Part4.Vin-
  N3: PDH1.connector14, BLDC4.Vin+
  N4: PDH1.connector15, BLDC4.Vin-
  N5: PDH1.connector16, Part3.Vin+
  N6: PDH1.connector17, Part3.Vin-
  N7: PDH1.connector18, BLDC3.Vin+
  N8: PDH1.connector19, BLDC3.Vin-
  N9: PDH1.connector20, BLDC1.Vin+
  N10: PDH1.connector21, BLDC1.Vin-
  N11: PDH1.connector22, Part1.Vin+
  N12: PDH1.connector25, BLDC2.Vin-
  N13: PDH1.connector26, Part2.Vin-
  N14: PDH1.connector27, Part2.Vin+
  N15: PDH1.connector44, BAT1.-
  N16: PDH1.connector45, CB1.2
  N17: PDH1.connector46, cntl1.connector40
  N18: PDH1.connector47, cntl1.connector39
  N19: PDH1.connector48, RPM1.connector0
  N20: PDH1.connector49, RPM1.connector1
  N21: PDH1.connector50, CANivore1.connector0
  N22: PDH1.connector51, CANivore1.connector1
  N23: PDH1.connector52, RPM2.connector0
  N24: PDH1.connector53, RPM2.connector1
  N25: Part1.CAN_Y_1, BLDC2.CANH1#3
  N26: Part1.CAN_G_1, BLDC2.CANL0
  N27: Part1.CAN_Y_2, BLDC1.CANH1#5
  N28: Part1.CAN_G_2, BLDC1.CANL1
  N29: Part1.Middle_Connector_Pin_Power_Out_Red, Connector1.connector0
  N30: Part1.Middle_Connector_Pin_Power_Out_Black, Connector1.connector1
  N31: Part1.Middle_Connector_Pin_Yellow, Connector1.connector3
  N32: Part1.Middle_Connector_Pin_Green, Connector1.connector4
  N33: BLDC1.CANL0, CANivore1.connector3
  N34: BLDC1.CANH1#3, CANivore1.connector2
  N35: BAT1.+, CB1.1
  N36: cntl1.connector142, CANivore1.connector4
  N37: cntl1.connector144, RPM2.connector3
  N38: RPM1.connector2, Connector6.connector0
  N39: RPM1.connector3, Connector6.connector1
  N40: RPM1.connector4, Part4.CAN_Y_1
  N41: RPM1.connector5, Part4.CAN_G_1
  N42: Part2.CAN_Y_1, BLDC3.CANH1#3
  N43: Part2.CAN_G_1, BLDC3.CANL0
  N44: Part2.CAN_Y_2, BLDC2.CANH1#5
  N45: Part2.CAN_G_2, BLDC2.CANL1
  N46: Part2.Middle_Connector_Pin_Power_Out_Red, Connector2.connector0
  N47: Part2.Middle_Connector_Pin_Power_Out_Black, Connector2.connector1
  N48: Part2.Middle_Connector_Pin_Yellow, Connector2.connector3
  N49: Part2.Middle_Connector_Pin_Green, Connector2.connector4
  N50: Part3.CAN_Y_1, BLDC4.CANH1#5
  N51: Part3.CAN_G_1, BLDC4.CANL1
  N52: Part3.CAN_Y_2, BLDC3.CANH1#5
  N53: Part3.CAN_G_2, BLDC3.CANL1
  N54: Part3.Middle_Connector_Pin_Power_Out_Red, Connector3.connector0
  N55: Part3.Middle_Connector_Pin_Power_Out_Black, Connector3.connector1
  N56: Part3.Middle_Connector_Pin_Yellow, Connector3.connector3
  N57: Part3.Middle_Connector_Pin_Green, Connector3.connector4
  N58: Part4.CAN_Y_2, BLDC4.CANH1#3
  N59: Part4.CAN_G_2, BLDC4.CANL0
  N60: Part4.Middle_Connector_Pin_Power_Out_Red, Connector4.connector0
  N61: Part4.Middle_Connector_Pin_Power_Out_Black, Connector4.connector1
  N62: Part4.Middle_Connector_Pin_Yellow, Connector4.connector3
  N63: Part4.Middle_Connector_Pin_Green, Connector4.connector4
  N64: RPM2.connector2, Router1.ETH_right
  N65: R1.Pin_0, Connector6.connector3
  N66: R1.Pin_1, Connector6.connector4

notes:
  BL
  BR
  FL
  FR
  120 Ohm resistor
  Pigeon 2.0

custom parts:
  WCP_Kraken_X60: The Kraken X60 is a brushless motor developed by WestCoast Products that has been designed to withstand the rigors of the FIRST Robotics Competition.
  CTRE Falcon 500: The Falcon 500 powered by Talon FX is a brushless motor with an integrated motor controller and high-resolution encoder, custom designed specifically for the FIRST Robotics Competition, through a collaboration between Cross the Road Electronics and VEX Robotics.
  Battery 12V: Battery Holders Various common sizes : AA, AAA, 20mm coin cell and 12mm coin cell.
  Thermal Circuit Breaker: Cooper Bussman P/N CB185-120, CB185F-120, CB285-120 CB285F-120, CB285120F or Optifuse P/N 153120, 253120
